# Fritzing sketch scale_wiring_diagram (saved by Fritzing 0.9.3b)
breadboards: 1

parts:
  Part1 = Photon
  LCD2 = LCD screen  # not connected
  J2 = screw terminal, 4 pins
  J6 = screw terminal, 4 pins
  X1 = DB9 Connector [package=db9]  # not connected

nets:
  N1: Part1.RX, J6.pin2
  N2: Part1.TX, J6.pin3
  N3: Part1.GND, J2.pin1, J6.pin1
  N4: Part1.VIN, J2.pin2, J6.pin4
  N5: Part1.D0, J2.pin3
  N6: Part1.D1, J2.pin4

notes:
  LCD Backpack
  GND
  VCC
  SDA
  SCL
  RS232 converter
  with male DB9
  VCC
  <--
  -->
  GND
